// Logisim project FA.circ as structural Verilog: 1 circuit, main circuit main
module main (
  input  CI,
  input  A,
  input  B,
  output carry,
  output soma
);

  wire and_1_out, and_2_out, and_3_out, xor_2_out;

  and and_1 (and_1_out, A, B);
  and and_2 (and_2_out, A, CI);
  or or_1 (carry, and_1_out, and_2_out, and_3_out);
  and and_3 (and_3_out, B, CI);
  xor xor_1 (soma, B, xor_2_out);
  xor xor_2 (xor_2_out, A, CI);
endmodule
