// Logisim project HA.circ as structural Verilog: 1 circuit, main circuit main
module main (
  input  A,
  input  B,
  output S___A_____B,
  output C___A___B
);

  xor xor_1 (S___A_____B, A, B);
  and and_1 (C___A___B, A, B, B);
endmodule
