// Logisim project conversor-7-seg.circ as structural Verilog: 1 circuit, main circuit main
module main (
  input  in0,
  input  in1,
  input  in2,
  output out_4,
  output out_5,
  output out_6,
  output out_7,
  output out_8,
  output out_9,
  output out_10
);

  segmentos_main A (.A(in0), .B(in1), .C(in2), .out_4(out_4));
  seg_b B (.A(in0), .B(in1), .C(in2), .out_4(out_5));
  seg_c C (.A(in0), .B(in1), .C(in2), .out_4(out_6));
  seg_d D (.A(in0), .B(in1), .C(in2), .out_4(out_7));
  seg_e E (.A(in0), .B(in1), .C(in2), .out_4(out_8));
  seg_f F (.A(in0), .B(in1), .C(in2), .out_4(out_9));
  seg_g G (.A(in0), .B(in1), .C(in2), .out_4(out_10));
endmodule
