// Logisim project segmentos.circ as structural Verilog: 7 circuits, main circuit main
module main (
  input  A,
  input  B,
  input  C,
  output out_4
);

  wire and_1_out, and_2_out, and_3_out, not_1_out, not_2_out, not_3_out, or_1_out;

  not not_1 (not_1_out, A);
  and and_1 (and_1_out, not_1_out, B);
  and and_2 (and_2_out, A, not_2_out);
  not not_2 (not_2_out, B);
  and and_3 (and_3_out, B, not_3_out);
  not not_3 (not_3_out, C);
  or or_1 (or_1_out, and_1_out, and_2_out);
  or or_2 (out_4, or_1_out, and_3_out);
endmodule

module seg_b (
  input  A,
  input  B,
  input  C,
  output out_4
);

  wire and_1_out, and_2_out, and_3_out, not_1_out, not_2_out, or_1_out;

  not not_1 (not_1_out, B);
  not not_2 (not_2_out, C);
  and and_1 (and_1_out, A, not_1_out);
  and and_2 (and_2_out, not_1_out, not_2_out);
  or or_1 (or_1_out, and_1_out, and_2_out);
  and and_3 (and_3_out, not_2_out, A);
  or or_2 (out_4, or_1_out, and_3_out);
endmodule

module seg_c (
  input  A,
  input  B,
  input  C,
  output out_4
);

  wire and_1_out, and_2_out, not_1_out, not_2_out, or_1_out;

  not not_1 (not_1_out, A);
  not not_2 (not_2_out, C);
  and and_1 (and_1_out, A, C);
  and and_2 (and_2_out, not_1_out, not_2_out);
  or or_1 (or_1_out, B, and_1_out);
  or or_2 (out_4, and_2_out, or_1_out);
endmodule

module seg_d (
  input  A,
  input  B,
  input  C,
  output out_4
);

  wire and_1_out, and_2_out, not_1_out, not_2_out, not_3_out, or_1_out;

  not not_1 (not_1_out, A);
  not not_2 (not_2_out, B);
  not not_3 (not_3_out, C);
  and and_1 (and_1_out, B, C);
  and and_2 (and_2_out, not_2_out, not_3_out);
  or or_1 (or_1_out, not_1_out, and_1_out);
  or or_2 (out_4, or_1_out, and_2_out);
endmodule

module seg_e (
  input  A,
  input  B,
  input  C,
  output out_4
);

  wire and_1_out, and_2_out, not_1_out, not_2_out;

  not not_1 (not_1_out, A);
  not not_2 (not_2_out, C);
  and and_1 (and_1_out, not_1_out, not_2_out);
  and and_2 (and_2_out, B, not_2_out);
  or or_1 (out_4, and_1_out, and_2_out);
endmodule

module seg_f (
  input  A,
  input  B,
  input  C,
  output out_4
);

  wire A_nBC_out, B_nC_out, nA_nC_out, nAB_out, not_1_out, not_2_out, not_3_out, or_1_out, or_2_out;

  not not_1 (not_1_out, A);
  not not_2 (not_2_out, B);
  not not_3 (not_3_out, C);
  and A_nBC (A_nBC_out, A, not_2_out, not_2_out, C);
  and nA_nC (nA_nC_out, not_1_out, not_3_out);
  and B_nC (B_nC_out, B, not_3_out);
  and nAB (nAB_out, not_1_out, B);
  or or_1 (or_1_out, A_nBC_out, nA_nC_out);
  or or_2 (or_2_out, B_nC_out, nAB_out);
  or or_3 (out_4, or_1_out, or_2_out);

  // Notes on the sheet:
  //   seg-f
  //   S = ~A~C + B~C + ~AB + A~BC
endmodule

module seg_g (
  input  A,
  input  B,
  input  C,
  output out_4
);

  wire not_1_out, or_1_out;

  not not_1 (not_1_out, B);
  or or_1 (or_1_out, A, C);
  or or_2 (out_4, or_1_out, not_1_out);

  // Notes on the sheet:
  //   seg-g
  //   S = C + A + ~B
endmodule
