// Logisim project somador-3b.circ as structural Verilog: 1 circuit, main circuit main
module main (
  input  A2,
  input  A1,
  input  A0,
  input  B2,
  input  B1,
  input  B0,
  output Carry,
  output S2,
  output S1,
  output S0
);

  wire main_2_carry, main_3_c___a___b;

  FA_main main_1 (.A(A2), .B(B2), .carry(Carry), .CI(main_2_carry), .soma(S2));
  FA_main main_2 (.A(A1), .B(B1), .carry(main_2_carry), .CI(main_3_c___a___b), .soma(S1));
  HA_main main_3 (.A(A0), .B(B0), .S___A_____B(S0), .C___A___B(main_3_c___a___b));
endmodule
