// Logisim project somador-sinc-3b.circ as structural Verilog: 1 circuit, main circuit main
module main (
  input  in_1,
  input  in_2,
  input  in_3,
  input  in_4,
  input  in_5,
  input  in_6
);

  wire clock_1_out, main_1_s0, main_1_s1, main_1_s2, main_2_out_5, main_2_out_6, main_2_out_7, main_3_out_4,
       main_3_out_5, main_3_out_6, main_3_out_7, main_3_out_8, main_3_out_9, main_3_out_10;

  somador_3b_main main_1 (
    .A2(in_1), .B2(in_6), .A1(in_2), .B1(in_5), .A0(in_3), .B0(in_4), .S2(main_1_s2), .S1(main_1_s1),
    .S0(main_1_s0));  // open: Carry
  Clock clock_1 (.out(clock_1_out));
  registrador_3b_main main_2 (
    .out_5(main_2_out_5), .out_6(main_2_out_6), .out_7(main_2_out_7), .in_2(main_1_s2), .in_3(main_1_s1),
    .in_4(main_1_s0), .CLK(clock_1_out));
  conversor_7_seg_main main_3 (
    .in0(main_2_out_5), .in1(main_2_out_6), .in2(main_2_out_7), .out_4(main_3_out_4), .out_5(main_3_out_5),
    .out_6(main_3_out_6), .out_7(main_3_out_7), .out_8(main_3_out_8), .out_9(main_3_out_9),
    .out_10(main_3_out_10));
  _7_Segment_Display u_7_segment_display_1 (
    .g(main_3_out_4), .f(main_3_out_5), .a(main_3_out_6), .b(main_3_out_7), .e(main_3_out_8),
    .d(main_3_out_9), .c(main_3_out_10));  // open: dp
endmodule
